# Fritzing sketch Pressure Cuff (saved by Fritzing 0.9.3b)
circuit board: 5.95776cm x 4.57011cm
breadboards: 1

parts:
  R2 = Resistor [tolerance=±5% resistance=10k package=THT]  # not connected
  R3 = Resistor [tolerance=±5% resistance=47 package=THT]  # not connected
  R4 = Resistor [tolerance=±5% resistance=1.5 package=THT]  # not connected
  R5 = Resistor [tolerance=±5% resistance=1.5 package=THT]  # not connected
  R6 = Resistor [tolerance=±5% resistance=47 package=THT]  # not connected
  R7 = Resistor [tolerance=±5% resistance=15 package=THT]  # not connected
  Part2 = Adafruit ADS1115 16Bit I2C ADC [part_number="Adafruit #1085"]
  Raspberry_Pi_1 = Raspberry Pi 3 [part_number=RPI-3-V1.2]
  J5 = Generic double row SMD male header - 8 pins [form="♂ (male)" package=THT]

nets:
  N1: Part2.AIN0, J5.pin4
  N2: Part2.SDA, Raspberry_Pi_1.GPIO2
  N3: Part2.SCL, Raspberry_Pi_1.GPIO3
  GND: Part2.GND, J5.GND
  3V3: Part2.VDD, Raspberry_Pi_1.3v3, Raspberry_Pi_1.3V3, J5.pin2

notes:
  Vs
  GND
  Vout
  Aout
  SCL
  3.3V
  SDA

custom parts:
  Adafruit ADS1115 16Bit I2C ADC: For microcontrollers without an analog-to-digital converter or when you want a higher-precision ADC, the ADS1115 provides 16-bit precision at 860 samples/second over I2C. The chip can be configured as 4 single-ended input channels, or two differential channels. As a nice bonus, it even includes a programmable gain amplifier, up to x16, to help boost up smaller single/differential signals to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
  Generic double row SMD male header - 8 pins: Generic double row SMD male header
